# Fritzing sketch attiny programmer (saved by Fritzing 0.9.3b)
stripboards: 1

parts:
  J1 = male pin header, 6 pins [form="♂ (male)"]
  J2 = male pin header, 6 pins [form="♂ (male)"]
  IC1 = IC, DIP package, 8 pins [chip_label=ATTiny]
  LED2 = LED - 3mm [color="White (8000K)" package="3 mm [THT]"]
  LED3 = LED - 3mm [color="White (8000K)" package="3 mm [THT]"]

nets:
  N1: J1.pin2, IC1.pin7
  N2: J1.pin3, IC1.pin6
  N3: J1.pin4, IC1.pin5
  N4: J1.pin5, IC1.pin1
  N5: J1.pin6, LED2.anode
  N6: J2.pin5, IC1.pin8
  N7: J2.pin6, IC1.pin4, LED2.cathode, LED3.cathode
  N8: IC1.pin3, LED3.anode
