# Fritzing sketch attiny_cartografia (saved by Fritzing 0.9.3b)
circuit board: 4.9cm x 2.9cm
perfboards: 1

parts:
  U1 = ATTINY45 [package=dip]
  R1 = Resistor [tolerance=±5% resistance=690 package=THT]
  R2 = Resistor [tolerance=±5% resistance=690 package=THT]
  R3 = Resistor [tolerance=±5% resistance=690 package=THT]
  R0 = Resistor [tolerance=±5% resistance=690 package=THT]
  Part1 = LilyPad Coin Cell Battery Holder
  JP2 = Header 1 [package=1x01_offset]
  JP3 = Header 1 [package=1x01_offset]
  JP4 = Header 1 [package=1x01_offset]
  JP5 = Header 1 [package=1x01_offset]

nets:
  N1: U1.PB3(ADC3), R3.Pin_0
  N2: U1.GND, Part1.-
  N3: U1.PB0(MOSI), R0.Pin_0
  N4: U1.PB1(MISO), R1.Pin_0
  N5: U1.PB2(SCK_ADC1), R2.Pin_0
  N6: U1.VCC, Part1.+
  N7: R1.Pin_1, JP3.1
  N8: R2.Pin_1, JP4.1
  N9: R3.Pin_1, JP5.1
  N10: R0.Pin_1, JP2.1
