# Fritzing sketch attiny_trinket (saved by Fritzing 0.9.3b)
stripboards: 2

parts:
  IC2 = IC, DIP package, 8 pins [chip_label=IC]
  LED6 = LED - 3mm [color="White (4500K)" package="3 mm [THT]"]
  LED7 = LED - 3mm [color="White (4500K)" package="3 mm [THT]"]
  LED8 = LED - 3mm [color="White (4500K)" package="3 mm [THT]"]
  LED9 = LED - 3mm [color="White (4500K)" package="3 mm [THT]"]
  LED10 = LED - 3mm [color="White (4500K)" package="3 mm [THT]"]
  J4 = male pin header, 2 pins [form="♂ (male)"]

nets:
  N1: IC2.pin4, LED8.cathode
  N2: LED6.cathode, LED7.cathode
  N3: LED9.cathode, LED10.cathode, J4.pin2

notes:
  Bottom layer. Should be mirrored
  Vcc Gnd
